// Logisim project circuit_johnwarila.circ as structural Verilog: 1 circuit, main circuit main
module main (
);

  Button A ();  // open: out
  Button B ();  // open: out
  D_Flip_Flop d_ff_1 ();  // open: clk, D, Q, Qn, preset, en, reset
endmodule
